# Fritzing sketch Câblage proto (saved by Fritzing 0.6.3b)
breadboards: 1

parts:
  Arduino1 = Arduino
  LED1 = LED - 5mm [color="Red (633nm)" package="5 mm [THT]"]
  LED2 = LED - 5mm [color="Green (555nm)" package="5 mm [THT]"]
  J1 = Piezo Speaker

nets:
  N1: Arduino1.GND, LED1.cathode, LED2.cathode, J1.pin1
  N2: Arduino1.D13, LED1.anode
  N3: Arduino1.D12, LED2.anode
  N4: Arduino1.D11, J1.pin2
